# Fritzing sketch Blink (saved by Fritzing 0.7.12b)
breadboards: 1

parts:
  LED1 = LED - 5mm [color="Green (560nm)" package="5 mm [THT]"]
  R1 = Resistor [tolerance=±5% resistance=470 package=THT]
  Arduino1 = Arduino

nets:
  N1: LED1.cathode, Arduino1.GND
  N2: LED1.anode, R1.Pin_1
  N3: R1.Pin_0, Arduino1.D13
